# Fritzing sketch mrb23 (saved by Fritzing 0.9.10b)
breadboards: 3

parts:
  Nano1 = Arduino Nano v2.3
  Part1 = Arduino Uno (Rev3) - ICSP
  M1 = RioRand LM2596  # not connected
  C1 = Capacitor [package=cap-pth-small2]
  S1 = Pushbutton [package="[THT]"]
  LCD1 = LCD screen
  LCD2 = LCD screen
  U1 = PCF8574 [package="DIP16 [THT]"]
  U2 = POT [knob_status=50% power=0.5W package=pot_alpha_rv16af-20]
  U3 = POT [knob_status=50% power=0.5W package=pot_alpha_rv16af-20]
  U4 = POT [knob_status=50% power=0.5W package=pot_alpha_rv16af-20]
  U5 = POT [knob_status=50% power=0.5W package=pot_alpha_rv16af-20]
  R1 = Resistor [tolerance=±5% power=0.25 resistance=10k package=THT]
  R2 = Resistor [tolerance=±5% power=0.25 resistance=10k package=THT]
  R3 = Resistor [tolerance=±5% power=0.25 resistance=10k package=THT]
  R4 = Resistor [tolerance=±5% power=0.25 resistance=10k package=THT]
  R5 = Resistor [tolerance=±5% power=0.25 resistance=220 package=THT]
  R6 = Resistor [tolerance=±5% power=0.25 resistance=220 package=THT]
  R7 = Rotary Potentiometer (Large) [maximum_resistance=100kΩ knob_status=50% power=0.5W package=THT]
  M2 = DC Motor [voltage_(max)=6V voltage_(min)=3V]  # not connected
  L298N1 = L298N DC motor driver
  C2 = Capacitor [package=cap-pth-small2]
  C3 = Capacitor [package=cap-pth-small2]

nets:
  N1: Nano1.RST, S1.Pin_1
  GND: Nano1.GND, Part1.GND, C1.1, S1.Pin_3, LCD1.VSS, LCD1.R/W, LCD1.LED-, LCD2.RS, U1.P1, U1.P3, U1.GND, U2.A, U3.A, U4.A, U5.A, R6.Pin_0, R7.leg2, C2.1, C3.2
  N2: Nano1.D10, L298N1.IN2
  N3: Nano1.D11, L298N1.IN1
  N4: Nano1.D12, L298N1.ENA
  N5: Nano1.A6, R7.wiper
  N6: Nano1.A5, Part1.A5/SCL, LCD2.VDD, R1.Pin_1, R3.Pin_1
  N7: Nano1.A4, Part1.A4/SDA, LCD2.VSS, R2.Pin_1, R4.Pin_1
  N8: Nano1.A3, U2.S
  N9: Nano1.A2, U5.S
  N10: Nano1.A1, U4.S
  +5V: Nano1.A0, Nano1.+5V, Part1.5V, C1.2, LCD1.VDD, LCD2.V0, U1.A0, U1.A1, U1.A2, U1.P0, U1.P2, U2.E, U3.E, U4.E, U5.E, R1.Pin_0, R2.Pin_0, R3.Pin_0, R4.Pin_0, R5.Pin_0, R7.leg1, C2.2, C3.1
  N11: Part1.ICSP_MISO, Part1.D12/MISO, LCD1.RS
  N12: Part1.D11_PWM/MOSI, LCD1.E
  N13: Part1.D2, LCD1.DB7
  N14: Part1.D3_PWM, LCD1.DB6
  N15: Part1.D4, LCD1.DB5
  N16: Part1.D5_PWM, LCD1.DB4
  N17: LCD1.V0, R6.Pin_1
  N18: LCD1.LED+, R5.Pin_1

notes:
  Naar 12v 1.5A DC
  of 8*AA batterij ~12v

custom parts:
  L298N DC motor driver: 2x DC motor driver with 78M05 positive voltage regulator (7..35 V) L298N: max 46 V, 2 A Set 5 V Enable jumper to enable 5 V regultor (needed for the L298N) and +5 V output at screw terminal or supply external +5 V at screw terminal Set ENA and/or ENB to +5 V to enable motor permanently or supply ENA and/or ENB with PWM signal IN1 and IN2 set rotation directory for motor A (OUT1/OUT2) IN2 and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
